# Fritzing sketch Project_A_Skecth (saved by Fritzing 0.9.10b)
breadboards: 1

parts:
  VCC1 = Battery block 9V
  Mod1 = Raspberry Pi 4B
  M1 = gear-motor
  M2 = gear-motor
  M3 = gear-motor
  M4 = gear-motor
  IC1 = DIP - 12 pins [chip_label=TB6612 package="DIP (Dual Inline) [THT]"]  # not connected
  IC2 = DIP - 12 pins [chip_label=TB6612 package="DIP (Dual Inline) [THT]"]
  IC3 = DIP - 12 pins [chip_label=TB6612 package="DIP (Dual Inline) [THT]"]

nets:
  N1: VCC1.-, IC2.GND#1, IC3.GND#1
  N2: VCC1.+, IC2.VM(<12V), IC3.VM(<12V)
  VCC: Mod1.5V, IC2.VCC, IC3.VCC
  N3: Mod1.GND, Mod1.GPIO27, IC2.GND#10, IC3.PWM2, IC3.GND#10
  N4: Mod1.GPIO22, IC3.PWM1
  N5: Mod1.GPIO9, IC3.DIR2
  N6: Mod1.GPIO11, IC2.DIR1
  N7: Mod1.GPIO8, IC3.DIR1
  N8: Mod1.GPIO7, IC2.DIR2
  N9: Mod1.GPIO12, IC2.PWM2
  N10: Mod1.GPIO13, IC2.PWM1
  N11: M1.pin_1, IC3.M1-
  N12: M1.pin_2, IC3.M1+
  N13: M2.pin_1, IC2.M1-
  N14: M2.pin_2, IC2.M1+
  N15: M3.pin_1, IC2.M2+
  N16: M3.pin_2, IC2.M2-
  N17: M4.pin_1, IC3.M2+
  N18: M4.pin_2, IC3.M2-

notes:
  Motor: U_L
  Motor: U_R
  Motor: B_R
  Motor: B_L
  M1+
  M1-
  M2+
  M2-
  GND
  VM(<12V)
  DIR1
  PWM1
  PWM2
  DIR2
  GND
  VCC

custom parts:
  DIP - 12 pins: A DIP stand-in part for whatever IC you want. With 12 pins on a 300mil dual inline package (DIP) footprint.
